# Fritzing sketch BigEasyDriver_stepper_servo_Arduino (saved by Fritzing 0.9.4)

parts:
  U2 = Big Easy Driver ROB-11876 [part_number=ROB-11876]
  U1 = Arduino Uno (Rev3)
  M1 = Stepper Motor - Bipolar
  M2 = Basic Servo
  C1 = Electrolytic Capacitor [capacitance=10µF voltage=50V package="100 mil [THT, electrolytic]"]

nets:
  GND: U2.GND, U1.GND, M2.gnd, C1.-
  N1: U2.A#17, M1.A
  N2: U2.A#18, M1.C
  N3: U2.B#19, M1.B
  N4: U2.B#20, M1.D
  24V: U2.M+, C1.+
  N5: U2.ST, U1.D3_PWM
  N6: U2.DR, U1.D2
  N7: U1.D4, M2.pulse
  5V: M2.vcc

custom parts:
  Big Easy Driver ROB-11876: The Big Easy Driver, designed by Brian Schmalz, is a stepper motor driver board for bi-polar stepper motors up to 1.4A/phase. It is based on the Allegro A4988 stepper driver chip. It’s the next version of the popular Easy Driver board. Each Big Easy Driver can drive up to about 1.4A per phase of a bi-polar stepper motor. It is a chopper microstepping driver which defaults to 16 step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
